// Logisim project 4-bit Asynchronous down Counter with hexdisplay.circ as structural Verilog: 1 circuit, main circuit main
module main (
);

  wire clk_out;
  wire [3:0] FF0_q;

  Clock clk (.out(clk_out));
  T_Flip_Flop FF0 (.clk(clk_out), .T(1'b1), .Q(FF0_q[0]));  // open: Qn, preset, reset, en
  T_Flip_Flop FF1 (.clk(FF0_q[0]), .T(1'b1), .Q(FF0_q[1]));  // open: Qn, preset, reset, en
  T_Flip_Flop FF2 (.clk(FF0_q[1]), .T(1'b1), .Q(FF0_q[2]));  // open: Qn, preset, reset, en
  Hex_Digit_Display hex_digit_display_1 (.value(FF0_q));  // open: dp
  T_Flip_Flop FF3 (.clk(FF0_q[2]), .T(1'b1), .Q(FF0_q[3]));  // open: Qn, preset, reset, en
endmodule
