// Logisim project 4-bit Asynchronous down Counter.circ as structural Verilog: 1 circuit, main circuit main
module main (
  output Q3,
  output Q2,
  output Q1,
  output Q0
);

  wire clk_out;

  Clock clk (.out(clk_out));
  T_Flip_Flop FF0 (.clk(clk_out), .T(1'b1), .Q(Q0));  // open: Qn, preset, reset, en
  T_Flip_Flop FF1 (.clk(Q0), .T(1'b1), .Q(Q1));  // open: Qn, preset, reset, en
  T_Flip_Flop FF2 (.clk(Q1), .T(1'b1), .Q(Q2));  // open: Qn, preset, reset, en
  T_Flip_Flop FF3 (.clk(Q2), .T(1'b1), .Q(Q3));  // open: Qn, preset, reset, en
endmodule
