// Logisim project 4-bit Asynchronous up Counter  with hexdisplay.circ as structural Verilog: 1 circuit, main circuit main
module main (
);

  wire clk_out, FF0_qn, FF1_qn, FF2_qn;
  wire [3:0] FF0_q;

  Clock clk (.out(clk_out));
  T_Flip_Flop FF0 (.clk(clk_out), .T(1'b1), .Q(FF0_q[0]), .Qn(FF0_qn));  // open: preset, reset, en
  T_Flip_Flop FF1 (.clk(FF0_qn), .T(1'b1), .Q(FF0_q[1]), .Qn(FF1_qn));  // open: preset, reset, en
  T_Flip_Flop FF2 (.clk(FF1_qn), .T(1'b1), .Q(FF0_q[2]), .Qn(FF2_qn));  // open: preset, reset, en
  Hex_Digit_Display hex_digit_display_1 (.value(FF0_q));  // open: dp
  T_Flip_Flop FF3 (.clk(FF2_qn), .T(1'b1), .Q(FF0_q[3]));  // open: Qn, preset, reset, en
endmodule
