// Logisim project 4-bit Asynchronous up Counter.circ as structural Verilog: 1 circuit, main circuit main
module main (
  output Q3,
  output Q2,
  output Q1,
  output Q0
);

  wire clk_out, FF0_qn, FF1_qn, FF2_qn;

  Clock clk (.out(clk_out));
  T_Flip_Flop FF0 (.clk(clk_out), .T(1'b1), .Q(Q0), .Qn(FF0_qn));  // open: preset, reset, en
  T_Flip_Flop FF1 (.clk(FF0_qn), .T(1'b1), .Q(Q1), .Qn(FF1_qn));  // open: preset, reset, en
  T_Flip_Flop FF2 (.clk(FF1_qn), .T(1'b1), .Q(Q2), .Qn(FF2_qn));  // open: preset, reset, en
  T_Flip_Flop FF3 (.clk(FF2_qn), .T(1'b1), .Q(Q3));  // open: Qn, preset, reset, en
endmodule
