// Logisim project 4-bit Synchronous down Counter.circ as structural Verilog: 1 circuit, main circuit main
module main (
  output Q3,
  output Q2,
  output Q1,
  output Q0
);

  wire and_1_out, and_2_out, clk_out, FF0_qn, FF1_qn, FF2_qn;

  Clock clk (.out(clk_out));
  T_Flip_Flop FF0 (.clk(clk_out), .T(1'b1), .Q(Q0), .Qn(FF0_qn));  // open: preset, reset, en
  and and_1 (and_1_out, FF0_qn, FF1_qn);
  T_Flip_Flop FF1 (.clk(clk_out), .T(FF0_qn), .Q(Q1), .Qn(FF1_qn));  // open: preset, reset, en
  T_Flip_Flop FF2 (.clk(clk_out), .T(and_1_out), .Q(Q2), .Qn(FF2_qn));  // open: preset, reset, en
  and and_2 (and_2_out, and_1_out, FF2_qn);
  T_Flip_Flop FF3 (.clk(clk_out), .T(and_2_out), .Q(Q3));  // open: Qn, preset, reset, en
endmodule
