// Logisim project 4-bit Synchronous up Counter  with hexdisplay.circ as structural Verilog: 1 circuit, main circuit main
module main (
);

  wire and_1_out, and_2_out, clk_out;
  wire [3:0] FF0_q;

  Clock clk (.out(clk_out));
  T_Flip_Flop FF0 (.clk(clk_out), .T(1'b1), .Q(FF0_q[0]));  // open: Qn, preset, reset, en
  and and_1 (and_1_out, FF0_q[0], FF0_q[1]);
  T_Flip_Flop FF1 (.clk(clk_out), .T(FF0_q[0]), .Q(FF0_q[1]));  // open: Qn, preset, reset, en
  T_Flip_Flop FF2 (.clk(clk_out), .T(and_1_out), .Q(FF0_q[2]));  // open: Qn, preset, reset, en
  Hex_Digit_Display hex_digit_display_1 (.value(FF0_q));  // open: dp
  and and_2 (and_2_out, and_1_out, FF0_q[2]);
  T_Flip_Flop FF3 (.clk(clk_out), .T(and_2_out), .Q(FF0_q[3]));  // open: Qn, preset, reset, en
endmodule
